# Fritzing sketch fastled (saved by Fritzing 1.0.7)
breadboards: 1

parts:
  Part1 = Arduino Nano (Rev3.0)
  U1 = WS2812 RGB LED strip

nets:
  GND: Part1.GND, U1.GND
  N1: Part1.D6, U1.DIN
  5V: Part1.5V, U1.VCC

notes:
  WS2812B LED Strip

custom parts:
  WS2812 RGB LED strip: WS2812 strip
