# Fritzing sketch rgb_led (saved by Fritzing 1.0.8)
breadboards: 1

parts:
  Mod1 = Raspberry Pi Pico
  R1 = Resistor [tolerance=±5% resistance=220 package="1206 [SMD]"]
  R2 = Resistor [tolerance=±5% resistance=220 package="1206 [SMD]"]
  R3 = Resistor [tolerance=±5% resistance=220 package="1206 [SMD]"]
  LED1 = RGB LED (com. anode, rbg) [color="Red (633nm)" current=30mA package="5 mm [THT]"]

nets:
  N1: Mod1.pin_3, Mod1.pin_8, Mod1.pin_13, Mod1.pin_18, Mod1.pin_23, Mod1.pin_28, Mod1.pin_33, Mod1.pin_38
  N2: Mod1.pin_17, R1.Pin_1
  N3: Mod1.pin_19, R2.Pin_1
  N4: Mod1.pin_20, R3.Pin_1
  N5: Mod1.pin_36, LED1.common_anode
  N6: R1.Pin_0, LED1.red_cathode
  N7: R2.Pin_0, LED1.blue_cathode
  N8: R3.Pin_0, LED1.green_cathode

notes:
  3.3V
  Common anode RGB LED

custom parts:
  Raspberry Pi Pico: Raspberry Pi Pico. Based around the RP2040 microcontroller the Pico is a low cost microcontroller device bringing Raspberry Pi quality, cost, and easy of use to the microcontroller space. Jan 2021, Split part in to two versions: SMD (this one) and tht. This one is single sided and uses the castellation pads to solder the module to the board (no holes, other than for the USB connector!). The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
