# Fritzing sketch multiled (saved by Fritzing 0.9.2b)
breadboards: 1

parts:
  Part1 = Arduino Nano (Rev3.0)
  R1 = Resistor [tolerance=±5% resistance=220 package=THT]
  R2 = Resistor [tolerance=±5% resistance=220 package=THT]
  R3 = Resistor [tolerance=±5% resistance=220 package=THT]
  R4 = Resistor [tolerance=±5% resistance=220 package=THT]
  LED1 = LED - 3mm [color="Yellow (592nm)" package="3 mm [THT]"]
  LED2 = LED - 3mm [color="Red (635nm)" package="3 mm [THT]"]
  LED3 = LED - 3mm [color="Green (555nm)" package="3 mm [THT]"]
  LED4 = LED - 3mm [color="Blue (430nm)" package="3 mm [THT]"]

nets:
  N1: Part1.GND, LED1.cathode, LED2.cathode, LED3.cathode, LED4.cathode
  N2: Part1.D3, R4.Pin_1
  N3: Part1.D4, R3.Pin_1
  N4: Part1.D5, R2.Pin_1
  N5: Part1.D6, R1.Pin_1
  N6: R1.Pin_0, LED1.anode
  N7: R2.Pin_0, LED2.anode
  N8: R3.Pin_0, LED3.anode
  N9: R4.Pin_0, LED4.anode
