# Fritzing sketch multiled_mbed (saved by Fritzing 0.9.2b)
breadboards: 1

parts:
  R1 = Resistor [tolerance=±5% resistance=220 package=THT]
  R2 = Resistor [tolerance=±5% resistance=220 package=THT]
  R3 = Resistor [tolerance=±5% resistance=220 package=THT]
  R4 = Resistor [tolerance=±5% resistance=220 package=THT]
  LED1 = LED - 3mm [color="Yellow (592nm)" package="3 mm [THT]"]
  LED2 = LED - 3mm [color="Red (635nm)" package="3 mm [THT]"]
  LED3 = LED - 3mm [color="Green (555nm)" package="3 mm [THT]"]
  LED4 = LED - 3mm [color="Blue (430nm)" package="3 mm [THT]"]
  J2 = STM32 Nucleo boards

nets:
  N1: R1.Pin_0, LED1.anode
  N2: R1.Pin_1, J2.D7
  N3: R2.Pin_0, LED2.anode
  N4: R2.Pin_1, J2.D6_PWM
  N5: R3.Pin_0, LED3.anode
  N6: R3.Pin_1, J2.D5_PWM
  N7: R4.Pin_0, LED4.anode
  N8: R4.Pin_1, J2.D4
  N9: LED1.cathode, LED2.cathode, LED3.cathode, LED4.cathode, J2.GND

notes:
  NUCLEO-F401RE
