# Fritzing sketch multiled_esp32 (saved by Fritzing 0.9.2b)
breadboards: 1

parts:
  R1 = Resistor [tolerance=±5% resistance=220 package=THT]
  R2 = Resistor [tolerance=±5% resistance=220 package=THT]
  R3 = Resistor [tolerance=±5% resistance=220 package=THT]
  U1 = LuaNode32 / ESP32
  LED2 = LED - 3mm [color="Red (635nm)" package="3 mm [THT]"]
  LED4 = LED - 3mm [color="Blue (430nm)" package="3 mm [THT]"]
  LED3 = LED - 3mm [color="Green (555nm)" package="3 mm [THT]"]

nets:
  N1: R1.Pin_0, U1.D2
  N2: R1.Pin_1, LED3.cathode
  N3: R2.Pin_0, U1.D15
  N4: R2.Pin_1, LED2.cathode
  N5: R3.Pin_0, U1.D4
  N6: R3.Pin_1, LED4.cathode
  N7: U1.GND, LED2.anode, LED4.anode

notes:
  +
  GND

custom parts:
  LuaNode32 / ESP32: ESP32 based LuaNode32
